# Fritzing sketch Design (saved by Fritzing 0.9.3b)

parts:
  Raspberry_Pi_1 = Raspberry Pi 3 [part_number=RPI-3-V1.2]
  U1 = L298 [package=multiwatt15]
  U2 = L298 [package=multiwatt15]
  BAT1 = Battery Holders [package=battery-aa-panel]
  BAT2 = Battery Holders [package=battery-aa-panel]
  M2 = DC Motor
  M3 = DC Motor
  M4 = DC Motor
  M5 = DC Motor
  U3 = TRANSCHIPTC5747 [package=camera_sfv24r-2st_2]  # not connected

nets:
  N1: Raspberry_Pi_1.GPIO6, U2.IN1
  N2: Raspberry_Pi_1.GPIO13, U2.IN2
  N3: Raspberry_Pi_1.GPIO19, U2.IN3
  N4: Raspberry_Pi_1.GPIO26, U2.IN4
  N5: Raspberry_Pi_1.GPIO21, U1.IN2
  N6: Raspberry_Pi_1.GPIO20, U1.IN1
  N7: Raspberry_Pi_1.GPIO16, U1.IN4
  N8: Raspberry_Pi_1.GPIO12, U1.IN3
  N9: U1.OUT1, M5.pin_2
  N10: U1.OUT2, M5.pin_1
  N11: U1.OUT3, M2.pin_1
  N12: U1.OUT4, M2.pin_2
  N13: U2.OUT1, M3.pin_2
  N14: U2.OUT2, M3.pin_1
  N15: U2.VS, BAT2.+
  N16: U2.GND, BAT1.-
  N17: U2.OUT3, M4.pin_1
  N18: U2.OUT4, M4.pin_2
  N19: BAT1.+, BAT2.-

notes:
  右边为在上的接点
  set VS=VCC
